# Fritzing sketch MACCDC 2016 Badge (saved by Fritzing 0.9.2b)

parts:
  S1 = SPST Switch [package=switch-spdt]
  HUZZAH = HUZZAH ESP8266 Breakout
  CHARGER = PowerBoost 500 Charger
  OLED1 = 128x32 I2C Monochrome OLED Display
  BATTERY = LiPoly Battery (1300mAh)
  NEOPIXEL_STICK = Neopixel Strip -- Black (30/m)

nets:
  GND: S1.O, HUZZAH.GND, CHARGER.GND, OLED1.GND, BATTERY.negative, NEOPIXEL_STICK.GND
  N1: S1.P, CHARGER.ENABLE
  RX0/GPIO3: HUZZAH.RXD_5V
  RST: HUZZAH.GPIO16, OLED1.RST
  5V: HUZZAH.VBAT, CHARGER.5.0V, NEOPIXEL_STICK.+5V
  3.3V: HUZZAH.3.3V, OLED1.3.3V
  DI/TX1/GPIO2: HUZZAH.GPIO2, NEOPIXEL_STICK.Din
  SDA: HUZZAH.GPIO4, OLED1.SDA
  SCL: HUZZAH.GPIO5, OLED1.SCL
  N2: CHARGER.VBAT, BATTERY.positive

notes:
  2000/2500 mAh LiPo
  MACCDC 2016 Badge
  2000/2500 mAh

custom parts:
  HUZZAH ESP8266 Breakout: The ESP8266 processor from Espressif is an 80 MHz microcontroller with a full WiFi front-end (both as client and access point) and TCP/IP stack with DNS support as well.
  PowerBoost 500 Charger: The PowerBoost 500C is a little DC/DC boost converter module that can be powered by any 3.7V LiIon/LiPoly battery, and convert the battery output to 5.2V DC for running your 5V projects. At its heart is a TPS61090 boost converter from TI. This boost converter chip has some really nice extras such as low battery detection, 2A internal switch, synchronous conversion, excellent efficiency, and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
  LiPoly Battery (1300mAh): Lithium Ion Polymer Battery (1300mAh)
  Neopixel Strip -- Black (30/m): These NeoPixel strips have 30 digitally-addressable pixel LEDs per meter and are very affordable and are only 12.5 mm wide, 10 mm if you remove the strip from the casing.
